// Logisim project Chilis_CPU_logic_series.circ as structural Verilog: 8 circuits, main circuit main
module ALU8 (
  input  CONNECT_RS,
  input  CONNECT_LS,
  input  CONNECT_XOR,
  input  CONNECT_OR,
  input  CONNECT_AND,
  input  CONNECT_ADD,
  input  CONNECT_SUB,
  input  [7:0] DATA_IN2,
  input  [7:0] DATA_IN1,
  output [7:0] DATA_OUT,
  output CARRY_OUT,
  output ZERO_FLAG,
  output SIGN_FLAG
);

  wire adder_1_cout, left_shift_8_1_carry_out, or_1_out, right_shift_8_1_carry_out;
  wire [7:0] adder_1_out, and_1_out, bit_extender_1_out, left_shift_8_1_data_out, or_2_out,
       right_shift_8_1_data_out, xor_1_out, xor_2_out;

  assign bit_extender_1_out = {{7{CONNECT_SUB}}, CONNECT_SUB};  // Bit_Extender bit_extender_1
  assign xor_1_out = bit_extender_1_out ^ DATA_IN2;  // XOR_Gate xor_1, 8 bits wide
  or or_1 (or_1_out, CONNECT_ADD, CONNECT_SUB);
  assign DATA_OUT = or_1_out ? adder_1_out : 8'bz;  // Controlled_Buffer controlled_buffer_1
  Adder adder_1 (.a(xor_1_out), .b(DATA_IN1), .out(adder_1_out), .cin(CONNECT_SUB), .cout(adder_1_cout));
  assign and_1_out = xor_1_out & DATA_IN1;  // AND_Gate and_1, 8 bits wide
  assign or_2_out = xor_1_out | DATA_IN1;  // OR_Gate or_2, 8 bits wide
  assign xor_2_out = xor_1_out ^ DATA_IN1;  // XOR_Gate xor_2, 8 bits wide
  left_shift_8 left_shift_8_1 (
    .DATA_OUT(left_shift_8_1_data_out), .CARRY_OUT(left_shift_8_1_carry_out), .DATA_IN(DATA_IN1));
  right_shift_8 right_shift_8_1 (
    .CARRY_OUT(right_shift_8_1_carry_out), .DATA_OUT(right_shift_8_1_data_out), .DATA_IN(DATA_IN1));
  assign DATA_OUT = CONNECT_AND ? and_1_out : 8'bz;  // Controlled_Buffer controlled_buffer_2
  assign DATA_OUT = CONNECT_OR ? or_2_out : 8'bz;  // Controlled_Buffer controlled_buffer_3
  assign DATA_OUT = CONNECT_XOR ? xor_2_out : 8'bz;  // Controlled_Buffer controlled_buffer_4
  assign DATA_OUT = CONNECT_LS ? left_shift_8_1_data_out : 8'bz;  // Controlled_Buffer controlled_buffer_5
  assign CARRY_OUT = CONNECT_LS ? left_shift_8_1_carry_out : 1'bz;  // Controlled_Buffer controlled_buffer_6
  assign CARRY_OUT = or_1_out ? adder_1_cout : 1'bz;  // Controlled_Buffer controlled_buffer_7
  assign DATA_OUT = CONNECT_RS ? right_shift_8_1_data_out : 8'bz;  // Controlled_Buffer controlled_buffer_8
  assign CARRY_OUT = CONNECT_RS ? right_shift_8_1_carry_out : 1'bz;  // Controlled_Buffer controlled_buffer_9
  and and_2 (ZERO_FLAG, ~DATA_OUT[0], ~DATA_OUT[1], ~DATA_OUT[2], ~DATA_OUT[3], ~DATA_OUT[4], ~DATA_OUT[5], ~DATA_OUT[6], ~DATA_OUT[7]);  // AND_Gate

  assign SIGN_FLAG = DATA_OUT[7];
endmodule

module flipper_4_bit (
  input  [3:0] INPUT_NUMBER,
  input  FLIP_SWITCH,
  output [3:0] OUTPUT_NUMBER
);

  xor xor_1 (OUTPUT_NUMBER[3], INPUT_NUMBER[3], FLIP_SWITCH);
  xor xor_2 (OUTPUT_NUMBER[2], INPUT_NUMBER[2], FLIP_SWITCH);
  xor xor_3 (OUTPUT_NUMBER[1], INPUT_NUMBER[1], FLIP_SWITCH);
  xor xor_4 (OUTPUT_NUMBER[0], INPUT_NUMBER[0], FLIP_SWITCH);
endmodule

module left_shift_8 (
  input  [7:0] DATA_IN,
  output [7:0] DATA_OUT,
  output CARRY_OUT
);


  assign CARRY_OUT = DATA_IN[7];
  assign DATA_OUT = {DATA_IN[6:0], 1'b0};
endmodule

module right_shift_8 (
  input  [7:0] DATA_IN,
  output CARRY_OUT,
  output [7:0] DATA_OUT
);


  assign CARRY_OUT = DATA_IN[0];
  assign DATA_OUT = {1'b0, DATA_IN[7:1]};
endmodule

module main (
  input  CLEAR_MEM
);

  wire alu8_1_carry_out, alu8_1_sign_flag, alu8_1_zero_flag, and_1_out, and_2_out, and_3_out, and_4_out,
       and_5_out, and_6_out, and_7_out, and_8_out, and_9_out, and_10_out, and_11_out, and_12_out,
       clock_1_out, controlled_buffer_1_out, controlled_buffer_6_out, controlled_buffer_7_out,
       controlled_buffer_8_out, d_ff_1_q, d_ff_2_q, d_ff_6_q, decoder_1_out0, decoder_1_out1, decoder_1_out2,
       decoder_1_out3, decoder_1_out4, decoder_1_out5, decoder_1_out6, not_1_out, RESET_ALL_out, xnor_1_out,
       xor_1_out;
  wire [0:0] not_3_out, not_4_out;
  wire [2:0] controlled_buffer_2_out_2, controlled_buffer_2_out_3, controlled_buffer_2_out_4, d_ff_3_q;
  wire [7:0] A_q, alu8_1_data_out, B_q, controlled_buffer_11_out, counter_1_q, multiplexer_1_out,
       multiplexer_2_out, multiplexer_3_out, ram_1_dout;
  wire [7:2] register_1_q;
  wire [10:0] undriven;
  wire [20:0] controlled_buffer_2_out, not_2_out;
  wire [20:11] undriven_2, undriven_3, undriven_4;

  Button RESET_ALL (.out(RESET_ALL_out));
  Clock clock_1 (.out(clock_1_out));
  D_Flip_Flop d_ff_1 (.D(clock_1_out), .clk(RESET_ALL_out), .Q(d_ff_1_q));  // open: Qn, preset, reset
  xnor xnor_1 (xnor_1_out, d_ff_1_q, clock_1_out);
  Register A (.D(alu8_1_data_out), .en(controlled_buffer_2_out[0]), .clk(xnor_1_out), .Q(A_q), .clr(RESET_ALL_out));
  Register B (.D(alu8_1_data_out), .en(controlled_buffer_2_out[1]), .clk(xnor_1_out), .Q(B_q), .clr(RESET_ALL_out));
  Multiplexer #(.enable("false"), .select(3), .width(8)) multiplexer_1 (
    .in0(A_q), .in1(B_q), .in2(controlled_buffer_11_out), .out(multiplexer_1_out),
    .sel(controlled_buffer_2_out_3));  // open: in3, in4, in5, in6, in7
  Multiplexer #(.enable("false"), .select(3), .width(8)) multiplexer_2 (
    .in0(A_q), .in1(B_q), .in2({8{1'b0}}), .out(multiplexer_2_out), .sel(controlled_buffer_2_out_2));  // open: in3, in4, in5, in6, in7
  // Probe on {controlled_buffer_2_out[20:14], controlled_buffer_2_out_4, controlled_buffer_2_out[10:8], controlled_buffer_2_out_3, controlled_buffer_2_out_2, controlled_buffer_2_out[1:0]}
  Decoder #(.enable("false"), .select(3)) decoder_1 (
    .out0(decoder_1_out0), .out1(decoder_1_out1), .out2(decoder_1_out2), .out3(decoder_1_out3),
    .out4(decoder_1_out4), .out5(decoder_1_out5), .out6(decoder_1_out6), .sel(controlled_buffer_2_out[10:8]));  // open: out7
  Counter counter_1 (
    .load(controlled_buffer_2_out[15]), .D(alu8_1_data_out), .count(controlled_buffer_2_out[16]),
    .Q(counter_1_q), .clk(xnor_1_out), .clr(RESET_ALL_out));  // open: carry, up
  // Probe on multiplexer_1_out
  // Probe on multiplexer_2_out
  // Probe on alu8_1_data_out
  Multiplexer #(.enable("false"), .select(3), .width(8)) multiplexer_3 (
    .in0(A_q), .in1(B_q), .in2(counter_1_q), .out(multiplexer_3_out), .sel(controlled_buffer_2_out[19:17]));  // open: in3, in4, in5, in6, in7
  D_Flip_Flop d_ff_2 (
    .D(controlled_buffer_1_out), .clk(xnor_1_out), .Q(d_ff_2_q), .preset(RESET_ALL_out));  // open: Qn, reset
  assign controlled_buffer_1_out = and_2_out ? 1'b1 : 1'bz;  // Controlled_Buffer controlled_buffer_1
  ALU8 alu8_1 (
    .ZERO_FLAG(alu8_1_zero_flag), .SIGN_FLAG(alu8_1_sign_flag), .DATA_OUT(alu8_1_data_out),
    .CARRY_OUT(alu8_1_carry_out), .CONNECT_XOR(decoder_1_out4), .CONNECT_OR(decoder_1_out3),
    .CONNECT_AND(decoder_1_out2), .CONNECT_ADD(decoder_1_out0), .CONNECT_SUB(decoder_1_out1),
    .CONNECT_RS(decoder_1_out6), .CONNECT_LS(decoder_1_out5), .DATA_IN2(multiplexer_2_out),
    .DATA_IN1(multiplexer_1_out));
  RAM #(.clearpin("true"), .enables("line")) ram_1 (
    .addr(multiplexer_3_out), .we(not_1_out), .clk(xnor_1_out), .din(controlled_buffer_11_out),
    .dout(ram_1_dout), .clr(CLEAR_MEM));
  not not_1 (not_1_out, controlled_buffer_2_out[20]);
  assign {controlled_buffer_2_out[20:14], controlled_buffer_2_out_4, controlled_buffer_2_out[10:8], controlled_buffer_2_out_3, controlled_buffer_2_out_2, controlled_buffer_2_out[1:0]} = d_ff_2_q ? {10'h2a0, undriven} : 21'bz;  // Controlled_Buffer controlled_buffer_2
  and and_1 (and_1_out, d_ff_2_q, and_10_out);
  and and_2 (and_2_out, and_1_out, xor_1_out);
  and and_3 (and_3_out, d_ff_2_q, and_11_out);
  and and_4 (and_4_out, d_ff_2_q, and_12_out);
  // Probe on multiplexer_3_out
  not not_2 (not_2_out[0], not_2_out[1]);
  assign {controlled_buffer_2_out[20:14], controlled_buffer_2_out_4, controlled_buffer_2_out[10:8], controlled_buffer_2_out_3, controlled_buffer_2_out_2, controlled_buffer_2_out[1:0]} = and_2_out ? {not_2_out[20:11], {5{1'b0}}, not_2_out[5], 3'b010, not_2_out[1:0]} : 21'bz;  // Controlled_Buffer controlled_buffer_3
  assign {controlled_buffer_2_out[20:14], controlled_buffer_2_out_4, controlled_buffer_2_out[10:8], controlled_buffer_2_out_3, controlled_buffer_2_out_2, controlled_buffer_2_out[1:0]} = and_3_out ? {undriven_2, {11{1'b0}}} : 21'bz;  // Controlled_Buffer controlled_buffer_4
  assign {controlled_buffer_2_out[20:14], controlled_buffer_2_out_4, controlled_buffer_2_out[10:8], controlled_buffer_2_out_3, controlled_buffer_2_out_2, controlled_buffer_2_out[1:0]} = and_4_out ? {undriven_3, {11{1'b0}}} : 21'bz;  // Controlled_Buffer controlled_buffer_5
  assign controlled_buffer_6_out = controlled_buffer_2_out_4[2] ? alu8_1_zero_flag : 1'bz;  // Controlled_Buffer controlled_buffer_6
  assign controlled_buffer_7_out = controlled_buffer_2_out_4[1] ? alu8_1_carry_out : 1'bz;  // Controlled_Buffer controlled_buffer_7
  assign controlled_buffer_8_out = controlled_buffer_2_out_4[0] ? alu8_1_sign_flag : 1'bz;  // Controlled_Buffer controlled_buffer_8
  and and_5 (and_5_out, d_ff_2_q, ~controlled_buffer_1_out);  // AND_Gate
  assign controlled_buffer_1_out = and_3_out ? 1'b0 : 1'bz;  // Controlled_Buffer controlled_buffer_9
  assign controlled_buffer_1_out = and_4_out ? 1'b0 : 1'bz;  // Controlled_Buffer controlled_buffer_10
  D_Flip_Flop d_ff_3 (
    .D(controlled_buffer_6_out), .clk(xnor_1_out), .Q(d_ff_3_q[0]), .reset(RESET_ALL_out));  // open: Qn, preset
  D_Flip_Flop d_ff_4 (
    .D(controlled_buffer_7_out), .clk(xnor_1_out), .Q(d_ff_3_q[1]), .reset(RESET_ALL_out));  // open: Qn, preset
  D_Flip_Flop d_ff_5 (
    .D(controlled_buffer_8_out), .clk(xnor_1_out), .Q(d_ff_3_q[2]), .reset(RESET_ALL_out));  // open: Qn, preset
  assign controlled_buffer_11_out = controlled_buffer_2_out[14] ? alu8_1_data_out : 8'bz;  // Controlled_Buffer controlled_buffer_11
  xor xor_1 (xor_1_out, not_2_out[1], not_2_out[5]);
  and and_6 (and_6_out, and_1_out, ~xor_1_out);  // AND_Gate
  // Probe on controlled_buffer_11_out
  assign controlled_buffer_11_out = controlled_buffer_2_out[20] ? ram_1_dout : 8'bz;  // Controlled_Buffer controlled_buffer_12
  assign {controlled_buffer_2_out[20:14], controlled_buffer_2_out_4, controlled_buffer_2_out[10:8], controlled_buffer_2_out_3, controlled_buffer_2_out_2, controlled_buffer_2_out[1:0]} = and_6_out ? {undriven_4, {11{1'b0}}} : 21'bz;  // Controlled_Buffer controlled_buffer_13
  Register #(.trigger("falling")) register_1 (
    .D(controlled_buffer_11_out), .en(d_ff_2_q), .clk(xnor_1_out),
    .Q({register_1_q, not_2_out[1], not_2_out[5]}), .clr(RESET_ALL_out));
  D_Flip_Flop d_ff_6 (.D(and_5_out), .clk(xnor_1_out), .Q(d_ff_6_q), .reset(RESET_ALL_out));  // open: Qn, preset
  assign controlled_buffer_1_out = and_6_out ? 1'b0 : 1'bz;  // Controlled_Buffer controlled_buffer_14
  and and_7 (and_7_out, d_ff_6_q, and_10_out);
  assign controlled_buffer_1_out = and_7_out ? 1'b1 : 1'bz;  // Controlled_Buffer controlled_buffer_15
  and and_8 (and_8_out, d_ff_6_q, and_11_out);
  assign controlled_buffer_1_out = and_8_out ? 1'b1 : 1'bz;  // Controlled_Buffer controlled_buffer_16
  and and_9 (and_9_out, d_ff_6_q, and_12_out);
  assign controlled_buffer_1_out = and_9_out ? 1'b1 : 1'bz;  // Controlled_Buffer controlled_buffer_17
  // Probe on {register_1_q, not_2_out[1], not_2_out[5]}
  assign {controlled_buffer_2_out[20:14], controlled_buffer_2_out_4, controlled_buffer_2_out[10:8], controlled_buffer_2_out_3, controlled_buffer_2_out_2, controlled_buffer_2_out[1:0]} = and_7_out ? {19'h54012, not_2_out[1], not_4_out[0]} : 21'bz;  // Controlled_Buffer controlled_buffer_18
  not not_3 (not_3_out[0], not_2_out[1]);
  assign {controlled_buffer_2_out[20:14], controlled_buffer_2_out_4, controlled_buffer_2_out[10:8], controlled_buffer_2_out_3, controlled_buffer_2_out_2, controlled_buffer_2_out[1:0]} = and_8_out ? {3'b100, not_2_out[5], 15'h12, not_2_out[1], not_3_out[0]} : 21'bz;  // Controlled_Buffer controlled_buffer_19
  assign {controlled_buffer_2_out[20:14], controlled_buffer_2_out_4, controlled_buffer_2_out[10:8], controlled_buffer_2_out_3, controlled_buffer_2_out_2, controlled_buffer_2_out[1:0]} = and_9_out ? {3'b000, not_2_out[1], 11'h100, not_2_out[5], 5'b01000} : 21'bz;  // Controlled_Buffer controlled_buffer_20
  not not_4 (not_4_out[0], not_2_out[1]);
  and and_10 (and_10_out, ~register_1_q[2], ~register_1_q[3], ~register_1_q[4], ~register_1_q[6], ~register_1_q[7], ~register_1_q[5]);  // AND_Gate
  and and_11 (and_11_out, register_1_q[2], ~register_1_q[3], ~register_1_q[4], ~register_1_q[6], ~register_1_q[7], ~register_1_q[5]);  // AND_Gate
  and and_12 (and_12_out, ~register_1_q[2], register_1_q[3], ~register_1_q[4], ~register_1_q[6], ~register_1_q[7], ~register_1_q[5]);  // AND_Gate

  // Notes on the sheet:
  //   F-BUS
  //   A-BUS
  //   phase 1
  //   src
  //   dest
  //   mov r,[r]
  //   mov [r],r
  //   mov r,r / mov r,imm
  //   phase 2
  //   D-BUS
endmodule

module memory (
  input  in_1,
  input  [2:0] in_2,
  input  in_3,
  input  in_4,
  input  [7:0] in_5,
  input  in_6,
  output [7:0] out_7
);

  wire and_1_out, and_2_out, and_3_out, and_4_out, and_5_out, and_6_out, and_7_out, and_8_out, and_9_out,
       and_10_out, and_11_out, and_12_out, and_13_out, and_14_out, and_15_out, and_16_out, decoder_1_out0,
       decoder_1_out1, decoder_1_out2, decoder_1_out3, decoder_1_out4, decoder_1_out5, decoder_1_out6,
       decoder_1_out7;
  wire [7:0] register_1_q, register_2_q, register_3_q, register_4_q, register_5_q, register_6_q,
       register_7_q, register_8_q;

  Decoder #(.select(3)) decoder_1 (
    .out0(decoder_1_out0), .out1(decoder_1_out1), .out2(decoder_1_out2), .out3(decoder_1_out3),
    .out4(decoder_1_out4), .out5(decoder_1_out5), .out6(decoder_1_out6), .out7(decoder_1_out7), .sel(in_2),
    .en(in_1));
  and and_1 (and_1_out, ~in_3, decoder_1_out0);  // AND_Gate
  and and_2 (and_2_out, ~in_3, decoder_1_out1);  // AND_Gate
  and and_3 (and_3_out, ~in_3, decoder_1_out2);  // AND_Gate
  and and_4 (and_4_out, ~in_3, decoder_1_out3);  // AND_Gate
  and and_5 (and_5_out, ~in_3, decoder_1_out4);  // AND_Gate
  and and_6 (and_6_out, ~in_3, decoder_1_out5);  // AND_Gate
  and and_7 (and_7_out, ~in_3, decoder_1_out6);  // AND_Gate
  and and_8 (and_8_out, ~in_3, decoder_1_out7);  // AND_Gate
  Register register_1 (.D(out_7), .en(and_1_out), .clk(in_4), .Q(register_1_q));  // open: clr
  and and_9 (and_9_out, decoder_1_out0, in_3);
  Register register_2 (.D(out_7), .en(and_2_out), .clk(in_4), .Q(register_2_q));  // open: clr
  and and_10 (and_10_out, decoder_1_out1, in_3);
  Register register_3 (.D(out_7), .en(and_3_out), .clk(in_4), .Q(register_3_q));  // open: clr
  and and_11 (and_11_out, decoder_1_out2, in_3);
  Register register_4 (.D(out_7), .en(and_4_out), .clk(in_4), .Q(register_4_q));  // open: clr
  and and_12 (and_12_out, decoder_1_out3, in_3);
  Register register_5 (.D(out_7), .en(and_5_out), .clk(in_4), .Q(register_5_q));  // open: clr
  and and_13 (and_13_out, decoder_1_out4, in_3);
  Register register_6 (.D(out_7), .en(and_6_out), .clk(in_4), .Q(register_6_q));  // open: clr
  and and_14 (and_14_out, decoder_1_out5, in_3);
  Register register_7 (.D(out_7), .en(and_7_out), .clk(in_4), .Q(register_7_q));  // open: clr
  and and_15 (and_15_out, decoder_1_out6, in_3);
  Register register_8 (.D(out_7), .en(and_8_out), .clk(in_4), .Q(register_8_q));  // open: clr
  and and_16 (and_16_out, decoder_1_out7, in_3);
  assign out_7 = and_9_out ? register_1_q : 8'bz;  // Controlled_Buffer controlled_buffer_1
  assign out_7 = and_10_out ? register_2_q : 8'bz;  // Controlled_Buffer controlled_buffer_2
  assign out_7 = and_11_out ? register_3_q : 8'bz;  // Controlled_Buffer controlled_buffer_3
  assign out_7 = and_12_out ? register_4_q : 8'bz;  // Controlled_Buffer controlled_buffer_4
  assign out_7 = and_13_out ? register_5_q : 8'bz;  // Controlled_Buffer controlled_buffer_5
  assign out_7 = and_14_out ? register_6_q : 8'bz;  // Controlled_Buffer controlled_buffer_6
  assign out_7 = and_15_out ? register_7_q : 8'bz;  // Controlled_Buffer controlled_buffer_7
  assign out_7 = and_16_out ? register_8_q : 8'bz;  // Controlled_Buffer controlled_buffer_8
  assign out_7 = in_6 ? in_5 : 8'bz;  // Controlled_Buffer controlled_buffer_9

  // Notes on the sheet:
  //   read/write
  //   clock
endmodule

module toggle_flip_flop (
  input  DATA_IN,
  input  LOAD_TOGGLE,
  input  SAVE,
  input  CLOCK,
  output Q,
  output NOT_Q
);

  wire multiplexer_1_out;
  wire [0:0] and_1_out;

  and and_1 (and_1_out[0], LOAD_TOGGLE, ~SAVE);  // AND_Gate
  Multiplexer #(.enable("false"), .select(2)) multiplexer_1 (
    .in0(DATA_IN), .in1(NOT_Q), .in2(Q), .out(multiplexer_1_out), .sel({SAVE, and_1_out[0]}));  // open: in3
  D_Flip_Flop d_ff_1 (.D(multiplexer_1_out), .clk(CLOCK), .Q(Q), .Qn(NOT_Q));  // open: preset, reset
endmodule

module binary_counter (
  input  COUNT,
  input  CLOCK,
  input  [3:0] DATA_IN
);

  wire and_1_out, and_2_out, and_3_out, and_4_out, and_5_out, and_6_out, and_7_out, not_1_out,
       toggle_flip_flop_1_q, toggle_flip_flop_2_q, toggle_flip_flop_3_q, toggle_flip_flop_4_q;

  not not_1 (not_1_out, COUNT);
  and and_1 (and_1_out, ~COUNT, ~not_1_out);  // AND_Gate
  toggle_flip_flop toggle_flip_flop_1 (
    .Q(toggle_flip_flop_1_q), .LOAD_TOGGLE(COUNT), .SAVE(and_1_out), .DATA_IN(DATA_IN[0]), .CLOCK(CLOCK));  // open: NOT_Q
  and and_2 (and_2_out, COUNT, toggle_flip_flop_1_q);
  and and_3 (and_3_out, ~and_2_out, ~not_1_out);  // AND_Gate
  toggle_flip_flop toggle_flip_flop_2 (
    .Q(toggle_flip_flop_2_q), .LOAD_TOGGLE(and_2_out), .SAVE(and_3_out), .DATA_IN(DATA_IN[1]), .CLOCK(CLOCK));  // open: NOT_Q
  and and_4 (and_4_out, and_2_out, COUNT, toggle_flip_flop_2_q);
  and and_5 (and_5_out, ~and_4_out, ~not_1_out);  // AND_Gate
  toggle_flip_flop toggle_flip_flop_3 (
    .Q(toggle_flip_flop_3_q), .LOAD_TOGGLE(and_4_out), .SAVE(and_5_out), .DATA_IN(DATA_IN[2]), .CLOCK(CLOCK));  // open: NOT_Q
  and and_6 (and_6_out, COUNT, and_2_out, and_4_out, toggle_flip_flop_3_q);
  and and_7 (and_7_out, ~and_6_out, ~not_1_out);  // AND_Gate
  toggle_flip_flop toggle_flip_flop_4 (
    .Q(toggle_flip_flop_4_q), .LOAD_TOGGLE(and_6_out), .SAVE(and_7_out), .DATA_IN(DATA_IN[3]), .CLOCK(CLOCK));  // open: NOT_Q
endmodule
